# Fritzing sketch estufaSchemme (saved by Fritzing 0.9.3b)
breadboards: 1

parts:
  Part2 = Arduino Pro Mini (3.3V)
  J1 = Power Jack [package=power_jack_smd]  # not connected
  LCD1 = LCD screen
  J2 = Piezo Speaker
  U1 = TEMPERATURE-SENSOR [package=to-92]
  KY-1 = Keyes Relay [package=THT]
  U2 = POT [package=pot_alpha_rv16af-20]

nets:
  N1: Part2.A2, U1.ADJ
  N2: Part2.MISO, LCD1.RS
  N3: Part2.MOSI, LCD1.E
  N4: Part2.D5, LCD1.DB4
  VSS: LCD1.VSS, LCD1.R/W, LCD1.LED-, U1.GND, KY-1.ground, U2.E
  VDD: LCD1.VDD, LCD1.LED+, J2.pin1, U1.VCC, KY-1.power, U2.A
  N5: LCD1.V0, U2.S

notes:
  9v
  10 K

custom parts:
  Keyes Relay: The Keyes 5V relay module is suitable for SCM development, home appliance control. It uses a 5V~12V TIL control signal which can control DC / AC signal.
